# Fritzing sketch SMPlayer_Fritzing_v1.1 (saved by Fritzing 0.9.2b)
circuit board: 7.10752cm x 5.75723cm
breadboards: 1

parts:
  Part1 = Arduino Pro Mini v13
  LED1 = RGB LED (com. cathode, rgb) [package="5 mm [THT]"]
  LED2 = RGB LED (com. cathode, rgb) [package="5 mm [THT]"]
  J1 = Piezo Speaker
  S1 = Pushbutton [package="[THT]"]
  S2 = Pushbutton [package="[THT]"]
  S3 = Pushbutton [package="[THT]"]
  R1 = Resistor [tolerance=±5% resistance=10k package=THT]
  R2 = Resistor [tolerance=±5% resistance=10k package=THT]
  R3 = Resistor [tolerance=±5% resistance=10k package=THT]
  U1 = POT [package=alps_pot]
  R4 = Resistor [tolerance=±5% resistance=220 package=THT]
  R5 = Resistor [tolerance=±5% resistance=220 package=THT]

nets:
  N1: Part1.VCC, S1.Pin_3, S1.Pin_4, S2.Pin_3, S2.Pin_4, S3.Pin_3, S3.Pin_4
  N2: Part1.GND, J1.pin1, R1.Pin_0, R2.Pin_0, R3.Pin_0, R4.Pin_0, R5.Pin_0
  N3: Part1.D9_PWM, S1.Pin_1, S1.Pin_2, R1.Pin_1
  N4: Part1.D8, S2.Pin_1, S2.Pin_2, R2.Pin_1
  N5: Part1.D7, S3.Pin_1, S3.Pin_2, R3.Pin_1
  N6: Part1.D6_PWM, U1.E
  N7: Part1.D5_PWM, LED1.red_anode
  N8: Part1.D4, LED2.blue_anode
  N9: LED1.common_cathode, R4.Pin_1
  N10: LED2.common_cathode, R5.Pin_1
  N11: J1.pin2, U1.S
